# Fritzing sketch schema meteo (saved by Fritzing 0.9.7b)
breadboards: 1

parts:
  LCD_i2c = LCD1602-I2C
  Arduino_UNO_R3 = Arduino Uno (Rev3)
  Composant1 = GY-BMEP280 Barometric Pressure Sensor - Breakout
  S1 = Taiway 100-SP-X-T1 SPDT Miniature Toggle Switch [part_number=100-SP-X-T1-0-0-B1-M1 package=THT]
  VCC1 = Battery

nets:
  GND: LCD_i2c.GND, Arduino_UNO_R3.GND, Composant1.GND, VCC1.-
  VCC: LCD_i2c.VCC, Arduino_UNO_R3.5V, Composant1.VCC
  N1: LCD_i2c.SDA, Arduino_UNO_R3.A4/SDA
  N2: LCD_i2c.SCL, Arduino_UNO_R3.A5/SCL
  N3: Arduino_UNO_R3.D10_PWM/SS, Composant1.CSB
  N4: Arduino_UNO_R3.D11_PWM/MOSI, Composant1.SDA
  N5: Arduino_UNO_R3.D12/MISO, Composant1.SDO
  N6: Arduino_UNO_R3.D13/SCK, Composant1.SCL
  N7: Arduino_UNO_R3.VIN, S1.L1
  N8: S1.COM, VCC1.+

custom parts:
  LCD1602-I2C: A standard character display, usually with 2x16 characters. Comes in many colors with LCM1602 IIC attached.
  GY-BMEP280 Barometric Pressure Sensor - Breakout: The BME280 is a chip which was originally designed for the next generation of smartphones. It is made up of a very accurate pressure sensor and an associated temperature sensor which helps calibrate the pressure readings. And just for fun they threw in a pretty solid humidity sensor in there as well! So with an I2C connection you have access to enough weather data to make some pretty good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

// code stored in the sketch: station meteo.ino
#include <SPI.h>
#include <Wire.h>
#include <Adafruit_BME280.h>
#include <Adafruit_Sensor.h>
#include <LiquidCrystal_I2C.h>

LiquidCrystal_I2C lcd(0x27,16,2);  
#define BME_SCK 13
#define BME_MISO 12
#define BME_MOSI 11
#define BME_CS 10
#define SEALEVELPRESSURE_HPA (1013.25)
Adafruit_BME280 bme; // I2C
//Adafruit_BME280 bme(BME_CS); // hardware SPI
//Adafruit_BME280 bme(BME_CS, BME_MOSI, BME_MISO, BME_SCK); // software S
int delayTime = 1000;
void setup() {
 lcd.init();
 lcd.backlight();
 lcd.setCursor(1,0);
 lcd.print("Salut Paulo !");
 lcd.setCursor(2,1);
 lcd.print("Station météo...");
 delay(3000);
//init capteurs
 Serial.begin(9600);
 while(!Serial);    // time to get serial running
 Serial.println(F("BME280 test"));
 unsigned status;
 // verif si ok I2C
 status = bme.begin(); 
   if (!status) {
        Serial.println("Je ne trouve pas le capteur, vérifiez le cablage, l'adresse, l'ID du capteur!");
        Serial.print("Capteur ID etait: 0x"); 
        Serial.println(bme.sensorID(),16);
        Serial.print("        ID of 0xFF probablement une mauvaise adresse, un BMP 180 ou BMP 085\n");
        Serial.print("   ID of 0x56-0x58 represente un BMP 280,\n");
        Serial.print("        ID of 0x60 represente un BME 280.\n");
        Serial.print("        ID of 0x61 represente un BME 680.\n");
        while (1) delay(10);
    }

 Serial.println("-- Test par defaut --");

}

void loop() {
    printValues();
    delay(delayTime);
} 

void printValues() {
    Serial.print("Temperature = ");
    Serial.print(bme.readTemperature());
    Serial.println(" °C");

    Serial.print("Pression = ");

    Serial.print(bme.readPressure() / 100.0F);
    Serial.println(" hPa");

    Serial.print("Approx. Altitude = ");
    Serial.print(bme.readAltitude(SEALEVELPRESSURE_HPA));
    Serial.println(" m");

    Serial.print("Humidite = ");
    Serial.print(bme.readHumidity());
    Serial.println(" %");

    Serial.println();
}
